// Logisim project teste.circ as structural Verilog: 2 circuits, main circuit main
module main (
  input  [3:0] in_1,
  input  HABILITA_GRAVACAO,
  output [5:0] FUNCT,
  output [4:0] SA,
  output [5:0] OPCODE,
  output [4:0] ORIGEM_2,
  output [4:0] ORIGEM_1
);

  wire clock_1_out, CLOCK__out, registerfile_1_p2, registerfile_1_p7, registerfile_1_p8;
  wire [15:11] mipsprogramrom_1_p2;
  wire [31:0] adder_1_out, mipsprogramrom_1_p1;

  Adder #(.width(32)) adder_1 (.a(mipsprogramrom_1_p1), .b(32'h4), .out(adder_1_out));  // open: cin, cout
  Clock clock_1 (.out(clock_1_out));
  // MIPSProgramROM mipsprogramrom_1: pin names not known; wires that end beside it: mipsprogramrom_1_p1, {OPCODE, ORIGEM_1, ORIGEM_2, mipsprogramrom_1_p2, SA, FUNCT}
  Register #(.width(32)) register_1 (.D(adder_1_out), .clk(clock_1_out), .Q(mipsprogramrom_1_p1));  // open: en, clr
  Clock #(.highDuration(8)) CLOCK_ (.out(CLOCK__out));
  // RegisterFile registerfile_1: pin names not known; wires that end beside it: CLOCK__out, registerfile_1_p2, HABILITA_GRAVACAO, mipsprogramrom_1_p2, ORIGEM_1, ORIGEM_2, registerfile_1_p7, registerfile_1_p8
  // Mips_ALU mips_alu_1: pin names not known; wires that end beside it: registerfile_1_p7, registerfile_1_p8, in_1, registerfile_1_p2

  // Notes on the sheet:
  //   MEMORIA DE PROGRAMA
  //   contents of mipsprogramrom_1 (hex, n*v repeats v):
  //   SUBU $8, $2, $13 ADDU $9, $8, $6
endmodule

module teste (
);

  wire [31:0] mipsprogramrom_1_p2;

  // MIPSProgramROM mipsprogramrom_1: pin names not known; wires that end beside it: {32{1'b0}}, mipsprogramrom_1_p2
endmodule
